# Fritzing sketch circuit (saved by Fritzing 0.9.4)
breadboards: 1

parts:
  Componente1 = GY-VL53L0XV2 Laser Ranger Module
  Arduino1 = Arduino Nano (Rev3.0)
  VCC1 = 4 x AAA Battery Mount
  J1 = Basic Servo
  J2 = Basic Servo
  M1 = fc-51 [package=THT]
  M2 = fc-51 [package=THT]
  C2 = Electrolytic Capacitor [capacitance=1000μF package="1010 [SMD, electrolytic]"]

nets:
  VCC: Componente1.VCC, Arduino1.5V, VCC1.-, J1.vcc, J2.vcc, M1.pin3, M2.pin3, C2.+
  GND: Componente1.GND, Arduino1.GND, VCC1.+, J1.gnd, J2.gnd, M1.pin2, M2.pin2, C2.-
  N1: Componente1.SCL, Arduino1.A5
  N2: Componente1.SDA, Arduino1.A4
  N3: Arduino1.D2, J2.pulse
  N4: Arduino1.D3, J1.pulse
  N5: Arduino1.D8, M2.pin1
  N6: Arduino1.D9, M1.pin1

notes:
  By Fritzen I/O
  Related example: https://github.com/fritzen/arduino-robot-due

custom parts:
  GY-VL53L0XV2 Laser Ranger Module: The GY-VL53L0XV2 is based on the VL53L0X from ST Microelectronics, a time-of-flight ranging system integrated into a compact module.

// code stored in the sketch: Button.ino
/*
  Button
 
 Turns on and off a light emitting diode(LED) connected to digital  
 pin 13, when pressing a pushbutton attached to pin 2. 
 
 
 The circuit:
 * LED attached from pin 13 to ground 
 * pushbutton attached to pin 2 from +5V
 * 10K resistor attached to pin 2 from ground
 
 * Note: on most Arduinos there is already an LED on the board
 attached to pin 13.
 
 
 created 2005
 by DojoDave <http://www.0j0.org>
 modified 30 Aug 2011
 by Tom Igoe
 
 This example code is in the public domain.
 
 http://www.arduino.cc/en/Tutorial/Button
 */

// constants won't change. They're used here to 
// set pin numbers:
const int buttonPin = 2;     // the number of the pushbutton pin
const int ledPin =  13;      // the number of the LED pin

// variables will change:
int buttonState = 0;         // variable for reading the pushbutton status

void setup() {
  // initialize the LED pin as an output:
  pinMode(ledPin, OUTPUT);      
  // initialize the pushbutton pin as an input:
  pinMode(buttonPin, INPUT);     
}

void loop(){
  // read the state of the pushbutton value:
  buttonState = digitalRead(buttonPin);

  // check if the pushbutton is pressed.
  // if it is, the buttonState is HIGH:
  if (buttonState == HIGH) {     
    // turn LED on:    
    digitalWrite(ledPin, HIGH);  
  } 
  else {
    // turn LED off:
    digitalWrite(ledPin, LOW); 
  }
}
