# Fritzing sketch protoboard (saved by Fritzing 0.9.10b)
breadboards: 1

parts:
  IC1 = L293D [package=THT]
  Componente1 = Arduino Nano (Rev3.0)
  R1 = Photocell (LDR) [package=THT]
  R2 = Photocell (LDR) [package=THT]
  BAT1 = BC9VPC [package=bc9vpc]
  M1 = gear-motor
  M2 = gear-motor

nets:
  N1: IC1.Enable_1, IC1.+Vmotor, IC1.Enable_2, IC1.+V, Componente1.5V
  N2: IC1.In_1, Componente1.D5
  N3: IC1.Out_1_(_Controlled_by_Enable_1_), M2.pin_2
  N4: IC1.0V, Componente1.GND, R1.pin_0, R2.pin_0, BAT1.V-
  N5: IC1.In_2, Componente1.D4
  N6: IC1.In_3, Componente1.D2
  N7: IC1.Out_3_(_Controlled_by_Enable_2_), M1.pin_2
  N8: IC1.Out_4_(_Controlled_by_Enable_2_), M1.pin_1
  N9: IC1.In_4, Componente1.D3
  N10: Componente1.VIN, BAT1.V+
  N11: Componente1.A1, R1.pin_1
  N12: Componente1.A0, R2.pin_1
