# Fritzing sketch scheme (saved by Fritzing 0.9.10b)

parts:
  Componente1 = ESP12E Motor Shield
  M1 = gear-motor
  M2 = gear-motor
  6xAA_Battery1 = 6xAA Battery
  M4 = Dagu DGServo 9g (Top view) [part_number=RS001B]  # not connected
  M3 = Dagu DGServo 9g (Top view) [part_number=RS001B]  # not connected
  Mod1 = Amica NodeMCU DEVKIT 1.0  # not connected

nets:
  N1: Componente1.VIN#74, Componente1.VM
  N2: Componente1.A-, M2.pin_2
  N3: Componente1.A+, M2.pin_1
  N4: Componente1.B-, M1.pin_2
  N5: Componente1.B+, M1.pin_1
  N6: Componente1.VIN#102, 6xAA_Battery1.Pin_2
  N7: Componente1.GND, 6xAA_Battery1.Pin_1

custom parts:
  ESP12E Motor Shield: ESP8266 WiFi Motor Drive Expansion Board For NodeMCU ESP-12E
  6xAA Battery: 6xAA battery
