# Fritzing sketch robot (saved by Fritzing 0.9.3b)
breadboards: 1

parts:
  U1 = ESP8266 NodeMCU LoLin module
  M2 = Dagu DGServo 9g (Top view) [part_number=RS001B]
  M3 = Dagu DGServo 9g (Top view) [part_number=RS001B]
  VCC1 = Battery block 9V

nets:
  N1: U1.D0, M3.pulse
  N2: U1.D1, M2.pulse
  VCC: U1.3V3, M2.vcc, M3.vcc
  GND: U1.GND, M2.gnd, M3.gnd, VCC1.-
  N3: U1.Vin, VCC1.+

custom parts:
  ESP8266 NodeMCU LoLin module: ESP8266 based NodeMCU
