# Fritzing sketch esquema (saved by Fritzing 0.9.10b)
breadboards: 1

parts:
  Q1 = pnp-Powertransistor [package="TO220 [THT]"]
  R1 = Photocell (LDR) [package=THT]
  M1 = gear-motor
  Q2 = pnp-Powertransistor [package="TO220 [THT]"]
  R2 = Photocell (LDR) [package=THT]
  M2 = gear-motor
  LED1 = LED - 3mm [color="Red (633nm)" current=0.030 package="3 mm [THT]"]
  R3 = Resistor [tolerance=±5% resistance=220 package="1206 [SMD]"]
  VCC1 = Battery block 9V
  D1 = Rectifier Diode [part_number=1N4001 package="300 mil [THT]"]  # not connected
  D2 = Rectifier Diode [part_number=1N4001 package="300 mil [THT]"]

nets:
  N1: Q1.base, Q2.base, R3.Pin_1, VCC1.+
  N2: Q1.collector, M1.pin_1, D2.cathode
  N3: Q1.emitter, R1.pin_0
  N4: R1.pin_1, M1.pin_2, R2.pin_1, M2.pin_2, LED1.cathode, VCC1.-, D2.anode
  N5: Q2.collector, M2.pin_1
  N6: Q2.emitter, R2.pin_0
  N7: LED1.anode, R3.Pin_0
