# Fritzing sketch esquema2 (saved by Fritzing 0.9.10b)
breadboards: 1

parts:
  Q1 = pnp-Powertransistor [package="TO220 [THT]"]
  R1 = Photocell (LDR) [package=THT]
  M1 = gear-motor
  R2 = Photocell (LDR) [package=THT]
  M2 = gear-motor
  R3 = Resistor [tolerance=±5% resistance=220 package="1206 [SMD]"]
  VCC3 = Battery
  Q2 = pnp-Powertransistor [package="TO220 [THT]"]
  LED1 = LED - 3mm [color="Red (633nm)" current=0.030 package="3 mm [THT]"]

nets:
  N1: Q1.base, VCC3.+, Q2.base, LED1.anode
  N2: Q1.collector, M1.pin_1
  N3: Q1.emitter, R1.pin_0
  N4: R1.pin_1, M1.pin_2, R2.pin_1, M2.pin_2, R3.Pin_1, VCC3.-
  N5: R2.pin_0, Q2.emitter
  N6: M2.pin_1, Q2.collector
  N7: R3.Pin_0, LED1.cathode

custom parts:
  Battery: Your standard 2x 18650 battery pack (7.4 Volts)
